# Fritzing sketch esp32cam-battery-01 (saved by Fritzing 0.9.10b)
breadboards: 1

parts:
  BAT1 = 18650 battery holder [package=battery-18650-kit]
  Mod1 = ESP32 - CAM
  U3 = Voltage Regulator - 3.3V [package="TO220 [THT]"]

nets:
  GND: BAT1.+, Mod1.GND, U3.GND
  N1: BAT1.-, U3.input_voltage
  N2: Mod1.3V3, U3.output_voltage

notes:
  LDO (low-dropout)
  Voltage regulator (3.3 V)

custom parts:
  18650 battery holder: 18650 Battery Holder identical to the dual battery version.
  ESP32 - CAM: The ESP32-CAM has a very competitive small-size camera module that can operate independently as a minimum system with a footprint of only 27*40.5*4.5mm and a deep sleep current of up to 6mA.
